# Fritzing sketch Obstacle Avoiding Bot Stage 1 (saved by Fritzing 0.9.2b)
breadboards: 1

parts:
  Part1 = Arduino Uno (Rev3)
  U1 = HC-SR04 [chip_label=IC package="SIP (Single Inline) [THT]"]

nets:
  N1: Part1.D12/MISO, U1.Trig, U1.Echo
  5V: Part1.5V, U1.Vcc
  GND: Part1.GND, U1.GND

custom parts:
  HC-SR04: HC-SR04 ultrasound distance sensor
